// Logisim project single cycle datapath.circ as structural Verilog: 6 circuits, main circuit 1 bit alu
module _1_bit_alu (
  input  A,
  input  B,
  input  Cin,
  input  Less,
  input  [2:0] ALU_op,
  input  B_Inv,
  output Result,
  output Set,
  output Cout
);

  wire and_1_out, multiplexer_1_out, nor_1_out, not_1_out, or_1_out, xor_1_out;

  not not_1 (not_1_out, B);
  Multiplexer multiplexer_1 (.in0(B), .in1(not_1_out), .out(multiplexer_1_out), .sel(B_Inv));  // open: en
  Adder #(.width(1)) adder_1 (.a(A), .b(multiplexer_1_out), .out(Set), .cin(Cin), .cout(Cout));
  and and_1 (and_1_out, A, B);
  or or_1 (or_1_out, A, B);
  xor xor_1 (xor_1_out, A, B);
  nor nor_1 (nor_1_out, A, B);
  Multiplexer #(.select(3)) multiplexer_2 (
    .in0(and_1_out), .in1(or_1_out), .in2(xor_1_out), .in3(nor_1_out), .in4(Set), .in5(Less), .out(Result),
    .sel(ALU_op));  // open: in6, in7, en

  // Notes on the sheet:
  //   When ALU_Op=100,and B_inv=0 , Perform Subtractor
  //   When ALU_OP=100,and B_inv=1,perform addition
endmodule

module _10bit_register (
  input  [1:0] Read_Register_1__RS,
  input  [1:0] Write_Register__RD,
  input  [9:0] Write_Data,
  input  RegWrite,
  input  CLK,
  input  [1:0] Read_Register_2__RT,
  output [9:0] Read_Data_1,
  output [9:0] Read_Data_2
);

  wire and_1_out, and_2_out, and_3_out, and_4_out, decoder_1_out0, decoder_1_out1, decoder_1_out2,
       decoder_1_out3;
  wire [9:0] _0_q, _1_q, _2_q, _3_q;

  Decoder #(.select(2), .enable("false")) decoder_1 (
    .out0(decoder_1_out0), .out1(decoder_1_out1), .out2(decoder_1_out2), .out3(decoder_1_out3),
    .sel(Write_Register__RD));
  and and_1 (and_1_out, decoder_1_out0, RegWrite);
  and and_2 (and_2_out, decoder_1_out1, RegWrite);
  and and_3 (and_3_out, decoder_1_out2, RegWrite);
  and and_4 (and_4_out, decoder_1_out3, RegWrite);
  Register #(.width(10)) _0 (.D(Write_Data), .en(and_1_out), .Q(_0_q), .clk(CLK));  // open: clr
  Register #(.width(10)) _1 (.D(Write_Data), .en(and_2_out), .Q(_1_q), .clk(CLK));  // open: clr
  Register #(.width(10)) _2 (.D(Write_Data), .en(and_3_out), .Q(_2_q), .clk(CLK));  // open: clr
  Register #(.width(10)) _3 (.D(Write_Data), .en(and_4_out), .Q(_3_q), .clk(CLK));  // open: clr
  Multiplexer #(.select(2), .width(10), .enable("false")) multiplexer_1 (
    .in0(_0_q), .in1(_1_q), .in2(_2_q), .in3(_3_q), .out(Read_Data_1), .sel(Read_Register_1__RS));
  Multiplexer #(.select(2), .width(10), .enable("false")) multiplexer_2 (
    .in0(_0_q), .in1(_1_q), .in2(_2_q), .in3(_3_q), .out(Read_Data_2), .sel(Read_Register_2__RT));
endmodule

module Jump (
  input  [9:0] PC,
  input  [9:0] Instruction,
  output [9:0] jump
);


  assign jump = {PC[9:6], Instruction[5:0]};
endmodule

module CPU (
  output [9:0] out_1,
  output [9:0] out_2,
  output [9:0] out_3,
  output [3:0] out_4,
  output [1:0] out_5,
  output [1:0] out_6,
  output [1:0] out_7,
  output [9:0] out_8,
  output [9:0] out_9,
  output [3:0] out_10
);

  wire button_1_out, CLK_out, control_unit_1_alu_src, control_unit_1_binv, control_unit_1_cin,
       control_unit_1_jump, control_unit_1_load, control_unit_1_memtoreg, control_unit_1_r_itype,
       control_unit_1_register_write, control_unit_1_store;
  wire [1:0] multiplexer_1_out;
  wire [2:0] control_unit_1_aluop;
  wire [9:0] adder_1_out, adder_2_out, jump_1_jump, multiplexer_2_out, multiplexer_3_out, ram_1_data,
       register_1_q;

  Register #(.width(10)) register_1 (
    .D(multiplexer_3_out), .Q(register_1_q), .clk(CLK_out), .clr(button_1_out));  // open: en
  Button button_1 (.out(button_1_out));
  Clock CLK (.out(CLK_out));
  Adder #(.width(10)) adder_1 (.a(register_1_q), .b(10'h1), .out(adder_1_out));  // open: cin, cout
  ROM #(.addrWidth(10), .dataWidth(10)) rom_1 (.addr(register_1_q), .data({out_4, out_5, out_6, out_7}));  // open: sel
  Control_Unit control_unit_1 (
    .a(out_4[0]), .b(out_4[1]), .c(out_4[2]), .d(out_4[3]), .R_IType(control_unit_1_r_itype),
    .Register_Write(control_unit_1_register_write), .ALU_src(control_unit_1_alu_src),
    .Cin(control_unit_1_cin), .Binv(control_unit_1_binv), .ALUop(control_unit_1_aluop[0]),
    .ALUop_2(control_unit_1_aluop[1]), .ALUop_3(control_unit_1_aluop[2]), .Store(control_unit_1_store),
    .Load(control_unit_1_load), .MemtoReg(control_unit_1_memtoreg), .Jump(control_unit_1_jump));
  Jump jump_1 (.PC(adder_1_out), .Instruction({out_4, out_5, out_6, out_7}), .jump(jump_1_jump));
  Multiplexer #(.width(2)) multiplexer_1 (
    .in0(out_7), .in1(out_7), .out(multiplexer_1_out), .sel(control_unit_1_r_itype));  // open: en
  _10bit_register u_10bit_register_1 (
    .Write_Data(out_8), .RegWrite(control_unit_1_register_write), .CLK(CLK_out), .Read_Data_1(out_2),
    .Read_Register_1__RS(out_6), .Read_Data_2(out_1), .Read_Register_2__RT(multiplexer_1_out),
    .Write_Register__RD(out_5));
  assign out_9 = {{8{1'b0}}, out_7};  // Bit_Extender bit_extender_1
  Adder #(.width(10)) adder_2 (.a(adder_1_out), .b(out_9), .out(adder_2_out));  // open: cin, cout
  Multiplexer #(.width(10)) multiplexer_2 (
    .in0(out_1), .in1(out_9), .out(multiplexer_2_out), .sel(control_unit_1_alu_src));  // open: en
  Multiplexer #(.width(10)) multiplexer_3 (
    .in0(adder_2_out), .in1(jump_1_jump), .out(multiplexer_3_out), .sel(control_unit_1_jump));  // open: en
  _10bitALU u_10bitalu_1 (
    .B(multiplexer_2_out), .A(out_2), .ALU_Op(control_unit_1_aluop), .result(out_3),
    .B_Inv(control_unit_1_binv), .Cin(control_unit_1_cin));  // open: zero, out_8
  RAM #(.addrWidth(10), .dataWidth(10), .bus("separate")) ram_1 (
    .addr(out_3), .din(out_1), .data(ram_1_data), .str(control_unit_1_store), .clk(CLK_out),
    .ld(control_unit_1_load));  // open: sel, clr
  Multiplexer #(.width(10)) multiplexer_4 (
    .in0(out_3), .in1(ram_1_data), .out(out_8), .sel(control_unit_1_memtoreg));  // open: en

  assign out_10 = out_4;

  // Notes on the sheet:
  //   contents of rom_1 (hex, n*v repeats v):
  //   39
endmodule

module _10bitALU (
  input  [9:0] B,
  input  [9:0] A,
  input  B_Inv,
  input  Cin,
  input  [2:0] ALU_Op,
  output [9:0] result,
  output zero,
  output out_8
);

  wire n1_bit_alu_1_cout, n1_bit_alu_2_cout, n1_bit_alu_3_cout, n1_bit_alu_4_cout, n1_bit_alu_5_cout,
       n1_bit_alu_6_cout, n1_bit_alu_6_set, n1_bit_alu_7_cout, n1_bit_alu_8_cout, n1_bit_alu_9_cout,
       n1_bit_alu_10_cout;

  _1_bit_alu u_1_bit_alu_1 (
    .A(A[0]), .B(B[0]), .Cin(Cin), .B_Inv(B_Inv), .Cout(n1_bit_alu_1_cout), .ALU_op(ALU_Op),
    .Result(result[0]), .Less(n1_bit_alu_6_set));  // open: Set
  _1_bit_alu u_1_bit_alu_2 (
    .A(A[1]), .B(B[1]), .Cin(n1_bit_alu_1_cout), .B_Inv(B_Inv), .Cout(n1_bit_alu_2_cout), .ALU_op(ALU_Op),
    .Result(result[1]), .Less(1'b0));  // open: Set
  _1_bit_alu u_1_bit_alu_3 (
    .A(A[2]), .B(B[2]), .Cin(n1_bit_alu_2_cout), .B_Inv(B_Inv), .Cout(n1_bit_alu_3_cout), .ALU_op(ALU_Op),
    .Result(result[2]), .Less(1'b0));  // open: Set
  _1_bit_alu u_1_bit_alu_4 (
    .A(A[3]), .B(B[3]), .Cin(n1_bit_alu_3_cout), .B_Inv(B_Inv), .Cout(n1_bit_alu_4_cout), .ALU_op(ALU_Op),
    .Result(result[3]), .Less(1'b0));  // open: Set
  _1_bit_alu u_1_bit_alu_5 (
    .A(A[4]), .B(B[4]), .Cin(n1_bit_alu_4_cout), .B_Inv(B_Inv), .Cout(n1_bit_alu_5_cout), .ALU_op(ALU_Op),
    .Result(result[4]), .Less(1'b0));  // open: Set
  _1_bit_alu u_1_bit_alu_6 (
    .A(A[5]), .B(B[5]), .Cin(n1_bit_alu_5_cout), .B_Inv(B_Inv), .Cout(n1_bit_alu_6_cout),
    .Set(n1_bit_alu_6_set), .ALU_op(ALU_Op), .Result(result[5]), .Less(1'b0));
  _1_bit_alu u_1_bit_alu_7 (
    .A(A[6]), .B(B[6]), .Cin(n1_bit_alu_6_cout), .B_Inv(B_Inv), .Cout(n1_bit_alu_7_cout), .ALU_op(ALU_Op),
    .Result(result[6]), .Less(1'b0));  // open: Set
  _1_bit_alu u_1_bit_alu_8 (
    .A(A[7]), .B(B[7]), .Cin(n1_bit_alu_7_cout), .B_Inv(B_Inv), .Cout(n1_bit_alu_8_cout), .ALU_op(ALU_Op),
    .Result(result[7]), .Less(1'b0));  // open: Set
  _1_bit_alu u_1_bit_alu_9 (
    .A(A[8]), .B(B[8]), .Cin(n1_bit_alu_8_cout), .B_Inv(B_Inv), .Cout(n1_bit_alu_9_cout), .ALU_op(ALU_Op),
    .Result(result[8]), .Less(1'b0));  // open: Set
  _1_bit_alu u_1_bit_alu_10 (
    .A(A[9]), .B(B[9]), .Cin(n1_bit_alu_9_cout), .B_Inv(B_Inv), .Cout(n1_bit_alu_10_cout),
    .Set(n1_bit_alu_6_set), .ALU_op(ALU_Op), .Result(result[9]), .Less(1'b0));
  xor xor_1 (out_8, n1_bit_alu_9_cout, n1_bit_alu_10_cout);
  nor nor_1 (zero, result[0], result[1], result[2], result[3], result[4], result[5], result[6], result[7], result[8], result[9]);
endmodule

module Control_Unit (
  input  a,
  input  b,
  input  c,
  input  d,
  output R_IType,
  output Register_Write,
  output ALU_src,
  output Cin,
  output Binv,
  output ALUop,
  output ALUop_2,
  output ALUop_3,
  output Store,
  output Load,
  output MemtoReg,
  output Jump
);

  wire and_2_out, and_3_out, and_4_out, and_5_out, not_1_out, not_2_out, not_3_out, not_4_out, not_5_out,
       not_6_out, not_7_out, not_8_out, not_9_out;

  and and_1 (ALU_src, b, not_1_out);
  not not_1 (not_1_out, c);
  not not_2 (not_2_out, b);
  and and_2 (and_2_out, not_2_out, c, d);
  and and_3 (and_3_out, b, not_3_out);
  not not_3 (not_3_out, c);
  not not_4 (not_4_out, b);
  and and_4 (and_4_out, not_4_out, c, not_5_out);
  not not_5 (not_5_out, d);
  not not_6 (not_6_out, c);
  and and_5 (and_5_out, b, not_6_out, not_7_out);
  not not_7 (not_7_out, d);
  and and_6 (Store, b, c, d);
  and and_7 (Load, b, c, not_8_out);
  not not_8 (not_8_out, d);
  and and_8 (MemtoReg, b, c, not_9_out);
  not not_9 (not_9_out, d);
  or or_1 (Cin, and_2_out, and_3_out);
  or or_2 (Binv, and_4_out, and_5_out);

  assign ALUop = b;
  assign ALUop_2 = c;
  assign ALUop_3 = d;
  assign Jump = 1'b0;
  assign R_IType = b;
  assign Register_Write = 1'b1;
endmodule
